// Logisim project COURSE_V1.1.circ as structural Verilog: 8 circuits, main circuit main
module main (
  input  in_1,
  input  in_2,
  input  in_3,
  input  in_4,
  input  _11_star,
  input  in_6,
  input  in_7,
  input  in_8,
  input  in_9,
  input  in_10,
  input  in_11,
  input  in_12,
  output out_13,
  output out_14,
  output out_15,
  output out_16,
  output out_17,
  output out_18,
  output out_19,
  output out_20
);

  wire adder_1_out_10, adder_1_out_11, adder_1_out_12, adder_1_out_13, adder_1_out_14, and_1_out, and_2_out,
       and_3_out, and_5_out, and_6_out, and_8_out, and_10_out, and_11_out, and_12_out, and_13_out,
       and_14_out, and_15_out, and_16_out, and_17_out, and_18_out, controller_1_out_3, controller_1_out_4,
       controller_1_out_5, multiplier_1_out_10, multiplier_1_out_11, multiplier_1_out_12,
       multiplier_1_out_13, multiplier_1_out_14, multiplier_1_out_15, multiplier_1_out_16,
       multiplier_1_result, not_1_out, subtractor_1_indicator, subtractor_1_out_10, subtractor_1_out_11,
       subtractor_1_out_12, subtractor_1_result;

  CONTROLLER controller_1 (
    .in_1(_11_star), .in_2(in_6), .out_3(controller_1_out_3), .out_4(controller_1_out_4),
    .out_5(controller_1_out_5));
  SUBTRACTOR subtractor_1 (
    .A(in_1), .in_2(in_2), .in_3(in_3), .in_4(in_4), .B(in_7), .in_6(in_8), .in_7(in_9), .in_8(in_10),
    .in_9(in_12), .out_10(subtractor_1_out_10), .out_11(subtractor_1_out_11), .out_12(subtractor_1_out_12),
    .RESULT(subtractor_1_result), .INDICATOR(subtractor_1_indicator));
  MULTIPLIER multiplier_1 (
    .A(in_1), ._3(in_2), ._2(in_3), ._1(in_4), .B(in_7), .in_6(in_8), .in_7(in_9), .in_8(in_10),
    .RESULT(multiplier_1_result), .out_10(multiplier_1_out_10), .out_11(multiplier_1_out_11),
    .out_12(multiplier_1_out_12), .out_13(multiplier_1_out_13), .out_14(multiplier_1_out_14),
    .out_15(multiplier_1_out_15), .out_16(multiplier_1_out_16));
  ADDER adder_1 (
    .A(in_1), .A___B(in_2), .in_3(in_3), .in_4(in_4), .B(in_7), .in_6(in_8), .in_7(in_9), .in_8(in_10),
    .in_9(in_11), .out_10(adder_1_out_10), .out_11(adder_1_out_11), .out_12(adder_1_out_12),
    .out_13(adder_1_out_13), .out_14(adder_1_out_14));
  not not_1 (not_1_out, subtractor_1_indicator);
  and and_1 (and_1_out, subtractor_1_indicator, controller_1_out_4);
  LED led_1 (.in(and_1_out));
  and and_2 (and_2_out, controller_1_out_3, controller_1_out_3, adder_1_out_10);
  and and_3 (and_3_out, controller_1_out_4, subtractor_1_out_10, not_1_out);
  and and_4 (out_13, controller_1_out_5, multiplier_1_result);
  and and_5 (and_5_out, controller_1_out_3, controller_1_out_3, adder_1_out_11);
  and and_6 (and_6_out, controller_1_out_4, subtractor_1_out_11, not_1_out);
  and and_7 (out_14, controller_1_out_5, multiplier_1_out_10);
  and and_8 (and_8_out, controller_1_out_4, subtractor_1_out_12, not_1_out);
  and and_9 (out_15, controller_1_out_5, multiplier_1_out_11);
  and and_10 (and_10_out, controller_1_out_3, adder_1_out_12);
  and and_11 (and_11_out, controller_1_out_5, multiplier_1_out_12);
  and and_12 (and_12_out, controller_1_out_3, adder_1_out_13);
  and and_13 (and_13_out, controller_1_out_4, subtractor_1_result, not_1_out);
  or or_1 (out_16, and_11_out, and_2_out);
  and and_14 (and_14_out, controller_1_out_3, adder_1_out_14);
  and and_15 (and_15_out, controller_1_out_5, multiplier_1_out_13);
  or or_2 (out_17, and_15_out, and_5_out, and_3_out);
  and and_16 (and_16_out, controller_1_out_5, multiplier_1_out_14);
  or or_3 (out_18, and_16_out, and_10_out, and_6_out);
  and and_17 (and_17_out, controller_1_out_5, multiplier_1_out_15);
  or or_4 (out_19, and_17_out, and_12_out, and_8_out);
  and and_18 (and_18_out, controller_1_out_5, multiplier_1_out_16);
  or or_5 (out_20, and_18_out, and_13_out, and_14_out);

  // Notes on the sheet:
  //      01 +
  //    10  -
  //   ERROR
endmodule

module FA (
  input  A,
  input  B,
  input  C,
  output RESULT,
  output CARRY
);

  wire and_1_out, and_2_out, and_3_out, and_4_out, and_5_out, and_6_out, and_7_out, and_8_out, not_1_out,
       not_2_out, not_3_out;

  not not_1 (not_1_out, A);
  not not_2 (not_2_out, B);
  not not_3 (not_3_out, C);
  and and_1 (and_1_out, A, not_2_out, not_3_out);
  and and_2 (and_2_out, B, not_1_out, not_3_out);
  and and_3 (and_3_out, C, not_2_out, not_1_out);
  and and_4 (and_4_out, C, B, A);
  and and_5 (and_5_out, C, B, not_1_out);
  and and_6 (and_6_out, B, A, not_3_out);
  and and_7 (and_7_out, A, A, C, not_2_out);
  and and_8 (and_8_out, C, B, A);
  or or_1 (RESULT, and_1_out, and_2_out, and_3_out, and_4_out);
  or or_2 (CARRY, and_5_out, and_6_out, and_7_out, and_8_out);

  // Notes on the sheet:
  //   A + B + C
endmodule

module HA (
  input  A,
  input  B,
  output RESULT,
  output CARRY
);

  wire not_1_out, or_1_out;

  or or_1 (or_1_out, B, A);
  and and_1 (CARRY, B, A);
  not not_1 (not_1_out, CARRY);
  and and_2 (RESULT, or_1_out, not_1_out);

  // Notes on the sheet:
  //   A + B
endmodule

module SUB (
  input  C,
  input  A,
  input  B,
  output ASK,
  output RESULT
);

  wire and_1_out, and_2_out, and_3_out, and_4_out, and_5_out, not_1_out, not_2_out, or_1_out, xor_1_out,
       xor_2_out;

  not not_1 (not_1_out, A);
  not not_2 (not_2_out, B);
  and and_1 (and_1_out, A, C);
  and and_2 (and_2_out, C, A, B);
  and and_3 (and_3_out, B, not_1_out);
  and and_4 (and_4_out, not_2_out, A);
  and and_5 (and_5_out, B, not_1_out);
  xor xor_1 (xor_1_out, and_1_out, C);
  xor xor_2 (xor_2_out, and_3_out, C);
  or or_1 (or_1_out, and_5_out, xor_1_out);
  xor xor_3 (RESULT, xor_2_out, and_4_out);
  or or_2 (ASK, and_2_out, or_1_out);

  // Notes on the sheet:
  //   A - B - C
endmodule

module MULTIPLIER (
  input  A,
  input  _3,
  input  _2,
  input  _1,
  input  B,
  input  in_6,
  input  in_7,
  input  in_8,
  output RESULT,
  output out_10,
  output out_11,
  output out_12,
  output out_13,
  output out_14,
  output out_15,
  output out_16
);

  wire and_1_out, and_2_out, and_3_out, and_4_out, and_5_out, and_6_out, and_7_out, and_8_out, and_9_out,
       and_10_out, and_11_out, and_12_out, and_13_out, and_14_out, and_15_out, fa_2_carry, fa_2_result,
       fa_3_carry, fa_4_carry, fa_4_result, fa_5_carry, fa_5_result, fa_6_carry, fa_6_result, fa_7_carry,
       fa_8_carry, ha_1_carry, ha_2_carry, ha_2_result, ha_3_carry, ha_3_result, ha_4_carry;

  and and_1 (and_1_out, B, A);
  FA fa_1 (.A(fa_3_carry), .B(fa_2_carry), .C(and_1_out), .RESULT(out_10), .CARRY(RESULT));
  and and_2 (and_2_out, B, _3);
  and and_3 (and_3_out, in_6, A);
  FA fa_2 (.A(fa_4_carry), .B(and_3_out), .C(and_2_out), .RESULT(fa_2_result), .CARRY(fa_2_carry));
  FA fa_3 (.A(ha_1_carry), .B(fa_5_carry), .C(fa_2_result), .RESULT(out_11), .CARRY(fa_3_carry));
  and and_4 (and_4_out, B, _2);
  and and_5 (and_5_out, in_7, A);
  and and_6 (and_6_out, in_6, _3);
  FA fa_4 (.A(ha_2_carry), .B(and_5_out), .C(and_6_out), .RESULT(fa_4_result), .CARRY(fa_4_carry));
  FA fa_5 (.A(fa_6_carry), .B(fa_4_result), .C(and_4_out), .RESULT(fa_5_result), .CARRY(fa_5_carry));
  HA ha_1 (.A(fa_7_carry), .B(fa_5_result), .RESULT(out_12), .CARRY(ha_1_carry));
  and and_7 (and_7_out, B, _1);
  and and_8 (and_8_out, in_6, _2);
  and and_9 (and_9_out, in_7, _3);
  and and_10 (and_10_out, in_8, A);
  HA ha_2 (.A(and_10_out), .B(and_9_out), .RESULT(ha_2_result), .CARRY(ha_2_carry));
  FA fa_6 (.A(ha_3_carry), .B(ha_2_result), .C(and_8_out), .RESULT(fa_6_result), .CARRY(fa_6_carry));
  FA fa_7 (.A(fa_8_carry), .B(fa_6_result), .C(and_7_out), .RESULT(out_13), .CARRY(fa_7_carry));
  and and_11 (and_11_out, in_6, _1);
  and and_12 (and_12_out, in_7, _2);
  and and_13 (and_13_out, in_8, _3);
  HA ha_3 (.A(and_13_out), .B(and_12_out), .RESULT(ha_3_result), .CARRY(ha_3_carry));
  FA fa_8 (.A(ha_4_carry), .B(ha_3_result), .C(and_11_out), .RESULT(out_14), .CARRY(fa_8_carry));
  and and_14 (and_14_out, in_8, _2);
  and and_15 (and_15_out, in_7, _1);
  HA ha_4 (.A(and_14_out), .B(and_15_out), .RESULT(out_15), .CARRY(ha_4_carry));
  and and_16 (out_16, in_8, _1);

  // Notes on the sheet:
  //   4
  //   A * B
endmodule

module SUBTRACTOR (
  input  A,
  input  in_2,
  input  in_3,
  input  in_4,
  input  B,
  input  in_6,
  input  in_7,
  input  in_8,
  input  in_9,
  output out_10,
  output out_11,
  output out_12,
  output RESULT,
  output INDICATOR
);

  wire sub_2_ask, sub_3_ask, sub_4_ask;

  SUB sub_1 (.C(sub_2_ask), .A(A), .B(B), .ASK(INDICATOR), .RESULT(out_10));
  SUB sub_2 (.C(sub_3_ask), .A(in_2), .B(in_6), .ASK(sub_2_ask), .RESULT(out_11));
  SUB sub_3 (.C(sub_4_ask), .A(in_3), .B(in_7), .ASK(sub_3_ask), .RESULT(out_12));
  SUB sub_4 (.C(in_9), .A(in_4), .B(in_8), .ASK(sub_4_ask), .RESULT(RESULT));

  // Notes on the sheet:
  //   A - B
endmodule

module ADDER (
  input  A,
  input  A___B,
  input  in_3,
  input  in_4,
  input  B,
  input  in_6,
  input  in_7,
  input  in_8,
  input  in_9,
  output out_10,
  output out_11,
  output out_12,
  output out_13,
  output out_14
);

  wire fa_2_carry, fa_3_carry, fa_4_carry;

  FA fa_1 (.A(fa_2_carry), .B(B), .C(A), .RESULT(out_11), .CARRY(out_10));
  FA fa_2 (.A(fa_4_carry), .B(A___B), .C(in_6), .RESULT(out_12), .CARRY(fa_2_carry));
  FA fa_3 (.A(in_9), .B(in_8), .C(in_4), .RESULT(out_14), .CARRY(fa_3_carry));
  FA fa_4 (.A(fa_3_carry), .B(in_7), .C(in_3), .RESULT(out_13), .CARRY(fa_4_carry));
endmodule

module CONTROLLER (
  input  in_1,
  input  in_2,
  output out_3,
  output out_4,
  output out_5
);

  wire not_1_out, not_2_out;

  not not_1 (not_1_out, in_1);
  not not_2 (not_2_out, in_2);
  and and_1 (out_3, in_2, not_1_out);
  and and_2 (out_4, in_1, not_2_out);
  and and_3 (out_5, in_2, in_1);
endmodule
